# Fritzing sketch StepperMotor (saved by Fritzing 0.9.6b)
breadboards: 1

parts:
  DRV_1 = DRV 8825 Stepper Motor Carrier, High Current [part_number="DRV 8825"]  # not connected
  M1 = RioRand LM2596  # not connected
  BAT1 = BC9VPC [package=bc9vpc]
  M2 = Stepper Motor - Bipolar  # not connected
  Mod1 = Raspberry Pi 4B
  C1 = Capacitor Polarized [package=cpol-radial-1000uf-63v]

nets:
  N1: BAT1.V+, BAT1.V-, Mod1.GND, C1.-
